// Logisim project labo3.circ as structural Verilog: 10 circuits, main circuit main
module main (
);

  ADDSUB_ALU ADDSUBALU ();  // open: Bit_2_Opcode_SIGNED, Bit_3_Opcode_SUB, A, B, C_out, R3, ZERO, OVERFLOW, R

  // Notes on the sheet:
  //   Attention, votre version de Logisim
  //   ne contient pas de tracker. Si vous
  //   enregistrez votre projet, toutes les
  //   informations du tracker seront
  //   définitivement effacées.
endmodule

module CUSTOM (
  input  [3:0] A,
  input  [3:0] B,
  input  in_3
);

  wire add1bit_1_c_out, add1bit_2_c_out, add1bit_3_c_out;
  wire [3:0] add1bit_1_d;

  ADD1BIT add1bit_1 (.A(A[0]), .B(A[1]), .D(add1bit_1_d[0]), .C_out(add1bit_1_c_out));  // open: C_in
  ADD1BIT add1bit_2 (.A(A[2]), .B(A[3]), .C_in(add1bit_1_c_out), .D(add1bit_1_d[1]), .C_out(add1bit_2_c_out));
  ADD1BIT add1bit_3 (.A(B[0]), .B(B[1]), .C_in(add1bit_2_c_out), .D(add1bit_1_d[2]), .C_out(add1bit_3_c_out));
  ADD1BIT add1bit_4 (.A(B[2]), .B(B[3]), .C_in(add1bit_3_c_out), .D(add1bit_1_d[3]));  // open: C_out

  // Notes on the sheet:
  //   Attention, votre version de Logisim
  //   ne contient pas de tracker. Si vous
  //   enregistrez votre projet, toutes les
  //   informations du tracker seront
  //   définitivement effacées.
endmodule

module ADD1BIT (
  input  A,
  input  B,
  input  C_in,
  output D,
  output C_out
);

  wire and_1_out, and_2_out, and_3_out, xor_1_out;

  xor xor_1 (xor_1_out, A, B);
  and and_1 (and_1_out, A, B);
  and and_2 (and_2_out, A, C_in);
  and and_3 (and_3_out, B, C_in);
  or or_1 (C_out, and_1_out, and_2_out, and_3_out);
  xor xor_2 (D, xor_1_out, C_in);

  // Notes on the sheet:
  //   Attention, votre version de Logisim
  //   ne contient pas de tracker. Si vous
  //   enregistrez votre projet, toutes les
  //   informations du tracker seront
  //   définitivement effacées.
endmodule

module ADDSUB_ALU (
  input  Bit_2_Opcode_SIGNED,
  input  Bit_3_Opcode_SUB,
  input  [3:0] A,
  input  [3:0] B,
  output OVERFLOW,
  output [3:0] R,
  output C_out,
  output R3,
  output ZERO
);

  wire bitselector_1_out, bitselector_2_out, overfaddsub_4bits_1_d;

  BitSelector #(.width(4)) bitselector_1 (.in(A), .out(bitselector_1_out), .sel(2'b11));
  BitSelector #(.width(4)) bitselector_2 (.in(B), .out(bitselector_2_out), .sel(2'b11));
  ADD_SUB4BITS add_sub4bits_1 (.Sub(Bit_3_Opcode_SUB), .A(A), .B(B), .D(R), .C_out(C_out));
  OVERFADDSUB_4BITS overfaddsub_4bits_1 (
    .Sub(Bit_3_Opcode_SUB), .A(bitselector_1_out), .B(bitselector_2_out), .R3(R3), .D(overfaddsub_4bits_1_d));
  Multiplexer #(.enable("false")) multiplexer_1 (
    .in0(overfaddsub_4bits_1_d), .in1(C_out), .out(OVERFLOW), .sel(Bit_2_Opcode_SIGNED));
  BitSelector #(.width(4)) bitselector_3 (.in(R), .out(R3), .sel(2'b11));
  ISZERO_4BITS iszero_4bits_1 (.A(R), .D(ZERO));

  // Notes on the sheet:
  //   Attention, votre version de Logisim
  //   ne contient pas de tracker. Si vous
  //   enregistrez votre projet, toutes les
  //   informations du tracker seront
  //   définitivement effacées.
endmodule

module ADD_SUB4BITS (
  input  Sub,
  input  [3:0] A,
  input  [3:0] B,
  output [3:0] D,
  output C_out
);

  wire [3:0] comp2_4bits_1_d;

  COMP2_4BITS comp2_4bits_1 (.S(Sub), .A(B), .D(comp2_4bits_1_d));
  ADD4BITS add4bits_1 (.A(A), .B(comp2_4bits_1_d), .D(D), .C_out(C_out));  // open: C_in

  // Notes on the sheet:
  //   Attention, votre version de Logisim
  //   ne contient pas de tracker. Si vous
  //   enregistrez votre projet, toutes les
  //   informations du tracker seront
  //   définitivement effacées.
endmodule

module ADD4BITS (
  input  [3:0] A,
  input  [3:0] B,
  input  C_in,
  output [3:0] D,
  output C_out
);

  wire add1bit_1_c_out, add1bit_2_c_out, add1bit_3_c_out;

  ADD1BIT add1bit_1 (.A(A[0]), .B(B[0]), .C_in(C_in), .D(D[0]), .C_out(add1bit_1_c_out));
  ADD1BIT add1bit_2 (.A(A[1]), .B(B[1]), .C_in(add1bit_1_c_out), .D(D[1]), .C_out(add1bit_2_c_out));
  ADD1BIT add1bit_3 (.A(A[2]), .B(B[2]), .C_in(add1bit_2_c_out), .D(D[2]), .C_out(add1bit_3_c_out));
  ADD1BIT add1bit_4 (.A(A[3]), .B(B[3]), .C_in(add1bit_3_c_out), .D(D[3]), .C_out(C_out));

  // Notes on the sheet:
  //   Attention, votre version de Logisim
  //   ne contient pas de tracker. Si vous
  //   enregistrez votre projet, toutes les
  //   informations du tracker seront
  //   définitivement effacées.
endmodule

module COMP2_4BITS (
  input  S,
  input  [3:0] A,
  output [3:0] D
);

  wire [3:0] xor_1_out;

  xor xor_1 (xor_1_out[0], S, A[0]);
  xor xor_2 (xor_1_out[1], S, A[1]);
  xor xor_3 (xor_1_out[2], S, A[2]);
  xor xor_4 (xor_1_out[3], S, A[3]);
  ADD4BITS add4bits_1 (.A(xor_1_out), .C_in(S), .D(D));  // open: B, C_out

  // Notes on the sheet:
  //   Attention, votre version de Logisim
  //   ne contient pas de tracker. Si vous
  //   enregistrez votre projet, toutes les
  //   informations du tracker seront
  //   définitivement effacées.
endmodule

module ISZERO_4BITS (
  input  [3:0] A,
  output D
);

  wire or_1_out, or_2_out;

  or or_1 (or_1_out, A[0], A[1]);
  or or_2 (or_2_out, A[2], A[3]);
  nor nor_1 (D, or_1_out, or_2_out);

  // Notes on the sheet:
  //   Attention, votre version de Logisim
  //   ne contient pas de tracker. Si vous
  //   enregistrez votre projet, toutes les
  //   informations du tracker seront
  //   définitivement effacées.
endmodule

module OVERFADDSUB_4BITS (
  input  Sub,
  input  A,
  input  B,
  input  R3,
  output D
);

  wire and_1_out, and_2_out, not_1_out, not_2_out, not_3_out, xor_1_out, xor_2_out;

  not not_1 (not_1_out, B);
  not not_2 (not_2_out, A);
  not not_3 (not_3_out, R3);
  xor xor_1 (xor_1_out, Sub, not_1_out);
  xor xor_2 (xor_2_out, B, Sub);
  and and_1 (and_1_out, not_2_out, xor_1_out, R3);
  and and_2 (and_2_out, A, xor_2_out, not_3_out);
  or or_1 (D, and_1_out, and_2_out);

  // Notes on the sheet:
  //   Attention, votre version de Logisim
  //   ne contient pas de tracker. Si vous
  //   enregistrez votre projet, toutes les
  //   informations du tracker seront
  //   définitivement effacées.
endmodule

module COMPARATEUR (
  input  Carry,
  input  R3,
  input  ZERO,
  input  [2:0] Opcode_2_0,
  input  A,
  input  B,
  output [3:0] Cmp
);

  wire and_1_out, and_2_out, bitselector_1_out, multiplexer_1_out, not_1_out, not_2_out, or_1_out,
       xnor_1_out, xor_1_out, xor_2_out;

  BitSelector #(.width(3)) bitselector_1 (.in(Opcode_2_0), .out(bitselector_1_out), .sel(2'b00));
  xor xor_1 (xor_1_out, bitselector_1_out, A);
  xor xor_2 (xor_2_out, bitselector_1_out, R3);
  and and_1 (and_1_out, xor_1_out, B);
  xnor xnor_1 (xnor_1_out, A, B);
  and and_2 (and_2_out, xor_2_out, xnor_1_out);
  or or_1 (or_1_out, and_1_out, and_2_out);
  not not_1 (not_1_out, ZERO);
  not not_2 (not_2_out, Carry);
  Multiplexer #(.select(3), .enable("false")) multiplexer_1 (
    .in1(or_1_out), .in2(or_1_out), .in3(not_1_out), .in4(ZERO), .in5(Carry), .in6(not_2_out),
    .out(multiplexer_1_out), .sel(Opcode_2_0));  // open: in0, in7
  ADD4BITS add4bits_1 (.A(4'b0000), .C_in(multiplexer_1_out), .D(Cmp));  // open: B, C_out

  // Notes on the sheet:
  //   Attention, votre version de Logisim
  //   ne contient pas de tracker. Si vous
  //   enregistrez votre projet, toutes les
  //   informations du tracker seront
  //   définitivement effacées.
endmodule
